# Fritzing sketch Untitled Sketch (saved by Fritzing 0.8.7b)
breadboards: 1

parts:
  Composant1 = Arduino Nano (Rev3.0)
  Composant2 = Adafruit_BMP280
  J1 = Piezo Speaker
  TP1 = TP4056 [chip_label=TP4056 package="DIP (Dual Inline) [THT]"]
  U2 = SWITCH_SPDT [package=kps-1290]
  U1 = LIPO-1000mAh [package=lipo-1000]

nets:
  GND: Composant1.GND, Composant2.GND, J1.pin1, TP1.pin6
  N1: Composant1.D6, J1.pin2
  N2: Composant1.VIN, U2.O
  5V: Composant1.5V, Composant2.VIN
  N3: Composant1.A5, Composant2.SCK/SCL
  N4: Composant1.A4, Composant2.SDI/SDA
  N5: TP1.pin3, U2.S
  N6: TP1.pin4, U1.+
  N7: TP1.pin5, U1.-

custom parts:
  Adafruit_BMP280: Bosch has stepped up their game with their new BMP280 sensor, an environmental sensor with temperature, barometric pressure that is the next generation upgrade to the BMP085/BMP180/BMP183. This sensor is great for all sorts of weather sensing and can even be used in both I2C and SPI! This precision sensor from Bosch is the best low-cost, precision sensing solution for measuring barometric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
  TP4056: A DIP stand-in part for whatever IC you want. With 6 pins on a 300mil dual inline package (DIP) footprint.
